// Digital circuit 74240.dig as structural Verilog
// Octal buffer/line driver; 3-state; inverting
module _74240 (
  input  _1A0,
  input  n1OE,
  input  _1A1,
  input  _1A2,
  input  _1A3,
  input  _2A0,
  input  n2OE,
  input  _2A1,
  input  _2A2,
  input  _2A3,
  input  VCC,
  input  GND,
  output _1Y0,
  output _1Y1,
  output _1Y2,
  output _1Y3,
  output _2Y0,
  output _2Y1,
  output _2Y2,
  output _2Y3
);

  wire not_1_out, not_2_out;

  not not_1 (not_1_out, n1OE);
  not not_2 (not_2_out, n2OE);
  Driver #(.invertDriverOutput("true")) driver_1 (.in(_1A0), .en(not_1_out));  // open: out
  Driver #(.invertDriverOutput("true")) driver_2 (.in(_1A1), .en(not_1_out));  // open: out
  Driver #(.invertDriverOutput("true")) driver_3 (.in(_1A2), .en(not_1_out));  // open: out
  Driver #(.invertDriverOutput("true")) driver_4 (.in(_1A3), .en(not_1_out));  // open: out
  Driver #(.invertDriverOutput("true")) driver_5 (.in(_2A0), .en(not_2_out));  // open: out
  Driver #(.invertDriverOutput("true")) driver_6 (.in(_2A1), .en(not_2_out));  // open: out
  Driver #(.invertDriverOutput("true")) driver_7 (.in(_2A2), .en(not_2_out));  // open: out
  Driver #(.invertDriverOutput("true")) driver_8 (.in(_2A3), .en(not_2_out));  // open: out
  PowerSupply powersupply_1 (.VDD(VCC), .GND(GND));

  // Notes on the sheet:
  //   _1A0: pin 2
  //   _1Y0: pin 18
  //   n1OE: pin 1
  //   _1A1: pin 4
  //   _1Y1: pin 16
  //   _1A2: pin 6
  //   _1Y2: pin 14
  //   _1A3: pin 8
  //   _1Y3: pin 12
  //   _2A0: pin 17
  //   _2Y0: pin 3
  //   n2OE: pin 19
  //   _2A1: pin 15
  //   _2Y1: pin 5
  //   _2A2: pin 13
  //   _2Y2: pin 7
  //   _2A3: pin 11
  //   _2Y3: pin 9
  //   VCC: pin 20, default 1
  //   GND: pin 10
endmodule
