// Digital circuit gigatron.dig as structural Verilog
module gigatron (
  input  Clock_25_MHz,
  input  [15:0] WriteBreakAddr,
  input  SingleStep,
  input  [15:0] BreakAddr,
  input  [7:0] X_Reg_Value,
  output [7:0] out_2,
  output [7:0] out_3,
  output [7:0] out_4,
  output [7:0] out_5,
  output [7:0] out_6,
  output [7:0] out_7,
  output [7:0] out_8,
  output [7:0] out_9,
  output [15:0] out_10,
  output [15:0] out_11,
  output [15:0] out_12,
  output [7:0] out_13,
  output [7:0] out_14,
  output [15:0] Trace_End_Address,
  output [7:0] InputValue,
  output [7:0] Keyboard,
  output [7:0] GamepadBtns
);

  wire and_1_out, and_2_out, and_3_out, and_4_out, Break, CLK1, CLK2, comparator_1_eq, comparator_2_eq,
       comparator_3_eq, DataBreakEnable_out, Disable_Breakpoint_out, EnableCLK_out, gigatroncpu_1_vga_hs,
       gigatroncpu_1_vga_vs, gigatronkeyboard_1_o, nIE, nLD, nOE_SRAM, not_2_out, nRST, nWE_SRAM, or_2_out,
       or_4_out, or_5_out, or_6_out, ProgramBreakEnable_out, RegXBreakEnable_out, Reset_out, ResetBtn_out,
       SER_DATA, SER_LATCH, SER_PULSE, SRAM_Write_Cycle_q, Trace_enable_out, VGACLK;
  wire [1:0] Clock_Devider_out;
  wire [3:0] gigatroncpu_1_vga_b, gigatroncpu_1_vga_g, gigatroncpu_1_vga_r;
  wire [7:0] EXOUT, INPUT, not_3_out, UP_out;
  wire [15:0] Trace_Write_Pointer_out;

  not not_1 (nLD, SER_LATCH);
  not not_2 (not_2_out, nIE);
  _74165 Gamepad (
    .pin1(nLD), .pin2(SER_PULSE), .pin3(GamepadBtns[4]), .pin4(GamepadBtns[5]), .pin5(GamepadBtns[6]),
    .pin6(GamepadBtns[7]), .pin8(1'b0), .pin9(SER_DATA), .pin10(1'b0), .pin11(GamepadBtns[0]),
    .pin12(GamepadBtns[1]), .pin13(GamepadBtns[2]), .pin14(GamepadBtns[3]), .pin15(1'b0), .pin16(1'b1));  // open: pin7
  Register #(.Bits(8)) Input_Register (.D(INPUT), .C(CLK2), .en(not_2_out), .Q(InputValue));
  DipSwitch DataBreakEnable (.out(DataBreakEnable_out));
  DipSwitch EnableCLK (.out(EnableCLK_out));
  DipSwitch #(.dipDefault("true")) Disable_Breakpoint (.out(Disable_Breakpoint_out));
  DipSwitch ProgramBreakEnable (.out(ProgramBreakEnable_out));
  DipSwitch RegXBreakEnable (.out(RegXBreakEnable_out));
  and and_1 (and_1_out, Break, Disable_Breakpoint_out);
  Comparator #(.Bits(16)) comparator_1 (.a(BreakAddr), .b(out_10), .eq(comparator_1_eq));  // open: gt, lt
  Comparator #(.Bits(16)) comparator_2 (.a(out_12), .b(WriteBreakAddr), .eq(comparator_2_eq));  // open: gt, lt
  and and_2 (and_2_out, EnableCLK_out, Clock_25_MHz, ~and_1_out);  // And
  Comparator #(.Bits(8)) comparator_3 (.a(out_5), .b(X_Reg_Value), .eq(comparator_3_eq));  // open: gt, lt
  or or_1 (VGACLK, and_2_out, SingleStep);
  or or_2 (or_2_out, ~RegXBreakEnable_out, comparator_3_eq);  // Or
  and and_3 (and_3_out, ProgramBreakEnable_out, or_2_out, comparator_1_eq);
  and and_4 (and_4_out, comparator_2_eq, ~nWE_SRAM, DataBreakEnable_out);  // And
  LED led_1 (.in(EXOUT[0]));
  LED led_2 (.in(EXOUT[1]));
  LED led_3 (.in(EXOUT[2]));
  LED led_4 (.in(EXOUT[3]));
  or or_3 (Break, and_3_out, and_4_out);
  Break break_1 (.brk(Break));
  Counter #(.Bits(2)) Clock_Devider (.en(1'b1), .C(VGACLK), .clr(1'b0), .out(Clock_Devider_out));  // open: ovf
  RS_FF_AS SRAM_Write_Cycle (.S(CLK2), .R(CLK1), .Q(SRAM_Write_Cycle_q));  // open: nQ
  Button RIGHT (.out(UP_out[0]));
  Button LEFT (.out(UP_out[1]));
  Button DOWN (.out(UP_out[2]));
  Button UP (.out(UP_out[3]));
  Button START (.out(UP_out[4]));
  Button SELECT (.out(UP_out[5]));
  Button B (.out(UP_out[6]));
  Button A (.out(UP_out[7]));
  gigatroncpu gigatroncpu_1 (
    .CLK1(CLK1), .CLK2(CLK2), .nRESET(nRST), .ROMDATA(out_11), .SRAMDATAREAD(out_13), .SER_DATA(SER_DATA),
    .ROMAddress(out_10), .EXOUT(EXOUT), .SRAMAddress(out_12), .SRAMDATAWRITE(out_13), .nOE_SRAM(nOE_SRAM),
    .nWE_SRAM(nWE_SRAM), .VGA_R(gigatroncpu_1_vga_r), .VGA_G(gigatroncpu_1_vga_g),
    .VGA_B(gigatroncpu_1_vga_b), .VGA_HS(gigatroncpu_1_vga_hs), .VGA_VS(gigatroncpu_1_vga_vs),
    .SER_PULSE(SER_PULSE), .SER_LATCH(SER_LATCH), .RegIR(out_2), .RegDR(out_3), .RegAccu(out_4),
    .RegX(out_5), .RegY(out_6), .RegOUT(out_7), .BUSValue(out_8), .ALUValue(out_9), .Input(INPUT), .nIE(nIE));
  DipSwitch Trace_enable (.out(Trace_enable_out));
  gigatronkeyboard gigatronkeyboard_1 (.nLD(nLD), .KCODE(Keyboard), .O(gigatronkeyboard_1_o));
  Counter #(.Bits(16)) Trace_Write_Pointer (
    .en(Trace_enable_out), .C(CLK2), .clr(1'b0), .out(Trace_Write_Pointer_out));  // open: ovf
  and and_5 (CLK1, ~Clock_Devider_out[1], ~Clock_Devider_out[0]);  // And
  or or_4 (or_4_out, SRAM_Write_Cycle_q, nWE_SRAM);
  assign not_3_out = ~UP_out;  // Not not_3, 8 bits wide
  and and_6 (CLK2, ~Clock_Devider_out[0], Clock_Devider_out[1]);  // And
  Multiplexer #(.Bits(8)) multiplexer_1 (
    .sel(gigatronkeyboard_1_o), .in_0(not_3_out), .in_1(Keyboard), .out(GamepadBtns));
  Register #(.Bits(16)) register_1 (
    .D(Trace_Write_Pointer_out), .C(CLK1), .en(Trace_enable_out), .Q(Trace_End_Address));
  or or_5 (or_5_out, or_4_out, ~nOE_SRAM);  // Or
  or or_6 (or_6_out, ~or_4_out, nOE_SRAM);  // Or
  EEPROM #(.AddrBits(16), .Bits(16)) ROM (.A(out_10), .CS(~1'b0), .WE(~1'b1), .OE(~1'b0), .D(out_11));
  RAMSinglePortSel #(.AddrBits(16), .Bits(8)) RAM (.A(out_12), .CS(~1'b0), .WE(~or_5_out), .OE(~or_6_out), .D(out_13));
  RAMSinglePortSel #(.AddrBits(16), .Bits(16)) Trace_Memory (
    .A(Trace_End_Address), .CS(Trace_enable_out), .WE(CLK1), .OE(1'b0), .D(out_10));
  and and_7 (nRST, Reset_out, ResetBtn_out);
  VGA vga_1 (
    .R(gigatroncpu_1_vga_r), .G(gigatroncpu_1_vga_g), .B(gigatroncpu_1_vga_b), .H(gigatroncpu_1_vga_hs),
    .V(gigatroncpu_1_vga_vs), .C(VGACLK));
  Button #(.activeLow("true")) ResetBtn (.out(ResetBtn_out));
  Reset Reset (.out(Reset_out));

  assign out_14 = out_13;

  // Other names for the same wires on the sheet: ALUValue[7:0] = out_9; BUSValue[7:0] = out_8; BTN0 = GamepadBtns[0];
  //   BTN1 = GamepadBtns[1]; BTN2 = GamepadBtns[2]; BTN3 = GamepadBtns[3]; BTN4 = GamepadBtns[4];
  //   BTN5 = GamepadBtns[5]; BTN6 = GamepadBtns[6]; BTN7 = GamepadBtns[7]; RegAccu[7:0] = out_4; RegDR[7:0] = out_3;
  //   RegIR[7:0] = out_2; RegOUT[7:0] = out_7; RegX[7:0] = out_5; RegY[7:0] = out_6; ROMAddress[15:0] = out_10;
  //   ROMData[15:0] = out_11; SRAMAddress[15:0] = out_12; SRAMDATAREAD[7:0] = out_13; SRAMDATAWRITE[7:0] = out_13

  // Notes on the sheet:
  //   Clock_25_MHz: Hz: 2147483647
  //   WriteBreakAddr: default 20
  //   BreakAddr: default 3345
  //   X_Reg_Value: default 20
  //   Clock
  //   CPU Status
  //   Input
  //   Debug
  //   Output
  //   CPU
  //   Gamepad
  //   Tracing
  //   Keyboard
  //   contents of ROM (hex, n*v repeats v):
  //   0,8018,c018,7fc1,7cc1,100,1d6,ff00,69,ca,c2,69,cec,ff00,69,ca
  //   ,61,15f0,101,6fc,82,ff00,c2,17ec,1a0,1,16ec,1a0,100,8018,c018
  //   ,0,18d2,19d6,601,26f4,8d,bf60,6c2,701,2bf4,681,c160,7c2,881,8c2
  //   ,1801,180,22ec,18d2,1901,180,22ec,19d6,300,8018,c018,ee00,16c2
  //   ,290,100,17d6,59dc,5fdc,2bdc,22dc,b4dc,e2dc,dc,dc,fcdc,dc,200
  //   ,5c2,ff00,ec2,fc2,10c2,11c2,12c2,700,8018,c018,0,c2,2c2,2cc2,f00
  //   ,8018,c018,13c2,14c2,114,3e0,2ec2,4800,21c2,0,1cc2,114,f9ca,f6ca
  //   ,f7ca,2cc2,1ac2,200,1bc2,f600,ac2,bc2,cc2,ad00,22c2,bd00,24c2
  //   ,f300,25c2,1601,2a0,16c2,7fc1,7cc1,1d01,314,cbe0,e800,2,2,314
  //   ,cbe0,f600,314,cbe0,f600,314,cbe0,f600,314,cbe0,f600,314,cbe0
  //   ,f600,314,cbe0,f600,314,cbe0,f600,314,cbe0,f600,314,cbe0,f600
  //   ,314,cbe0,f600,1414,5ce0,2a01,1414,94e0,2801,314,cbe0,f600,314
  //   ,cbe0,f600,314,cbe0,f600,1214,42e0,0,314,cbe0,f600,314,cbe0,f600
  //   ,314,cbe0,f600,314,cbe0,f600,314,cbe0,f600,314,cbe0,f600,314,cbe0
  //   ,f600,314,cbe0,f600,314,cbe0,f600,314,cbe0,f600,314,cbe0,f600
  //   ,314,cbe0,f600,314,cbe0,f600,314,cbe0,f600,314,cbe0,f600,314,cbe0
  //   ,f600,314,cbe0,f600,1414,27e0,1901,1414,e0,2515,1314,e0,1801,1314
  //   ,78e0,1901,f714,6ce0,1901,2,2,2419,2,314,cbe0,f500,18c3,0,19c2
  //   ,2,314,cbe0,f400,515,ffe0,7f00,c000,1fc2,8000,20c2,b300,9c2,100
  //   ,80c2,e81,ec2,761,f61,681,6c2,881,8c2,16e8,17fc,5360,6c60,781
  //   ,7c2,2d01,1df0,1efc,1a0,2f01,2dc2,22f0,23fc,0,100,2e81,27ec,28fc
  //   ,e800,2ce4,2ec2,4880,fe,48fc,f00,2ec2,48fc,1421,f00,700,300,100
  //   ,200,400,800,400,200,100,300,700,f00,e00,c00,800,400,200,100,200
  //   ,400,800,c00,e00,14c2,1000,dc2,e01,52f0,5500,1ec2,515,ffe0,2300
  //   ,1214,e0,114,2101,fb20,21c2,2c01,5cec,5dfc,0,f000,1441,14c2,2c01
  //   ,63f0,64fc,1a0,0,2cc2,1f19,201,2121,180,2019,2d6,7f00,fe29,fc89
  //   ,feca,8030,5,ff89,fd89,ffca,fc20,fb69,12,fa09,714,8d,7de8,7efc
  //   ,3f20,3f00,381,3c2,1301,1214,1f19,901,b1f4,280,9c2,bda0,8dec,da1
  //   ,4000,92fc,1fc2,91ec,c000,93fc,1fc2,1f01,2,4060,20c2,901,cf60
  //   ,9aec,9bfc,fc3,c0,901,620,a6f0,301,a400,1ec2,515,ffe0,3500,66fc
  //   ,1f19,f40,1421,13c2,3c0,af00,1ec2,515,ffe0,3300,66fc,1f19,25e0
  //   ,114,1101,ef60,beec,1201,1a0,12c2,7f20,c6f0,ee00,c5fc,c4fc,100
  //   ,bfec,1a0,2,8000,12c2,cbfc,2,16c2,100,17c2,200,5c2,1101,df60,e2ec
  //   ,b01,d5e8,a01,bc2,c01,ac2,dafc,f600,a00,bc2,ac2,2,cc2,3500,dcec
  //   ,1a0,2,11c2,eafc,0,201,320,2c2,ea00,1ec2,515,ffe0,2600,114,f909
  //   ,9c2,1fc2,f1ec,f2fc,100,ec00,dc2,201,2121,180,214,b1e0,8018,6*2
  //   ,aefc,201,ca00,dc2,114,911,d,de,20c2,d,1f91,2015,c000,160*5d,c018
  //   ,201,2121,180,8018,2d6,7f00,fe29,fc89,feca,8030,5,ff89,fd89,ffca
  //   ,fc20,fb69,12,fa09,714,8d,c4e8,c5fc,3f20,3f00,381,3c2,1301,dfd
  //   ,c018,d300,dc2,114,901,190,1f01,8d,afd,1fd2,dc00,dc2,301,f40,1421
  //   ,13c2,3c0,bfd,1f11,1f11,901,eea0,e5f0,f080,9c2,100,cfd,dc2,3c0
  //   ,e900,cfd,dc2,114,4e0,c000,2001,8080,20d2,1f01,a5,f4f0,1fc2,f6fc
  //   ,100,dc2,ff00,1ec2,515,ffe0,3c00,4*2,3fc,1715,1581,be8,15c2,1601
  //   ,280,16d2,d,de,fe,d,e80,ce4,1a0,114,1ee1,0,18c2,de,d,19c2,1601
  //   ,180,16c2,f600,1fc,12,5,414,13e0,18c2,b14,d2e0,12,180,1dc2,5,18c2
  //   ,1d11,5,19c2,1fc,f600,12,180,1dc2,1801,c6,1d11,1901,c6,1fc,f600
  //   ,1901,40ec,1dc2,1801,43f0,100,1dc2,d,fe,1d01,45ec,48f0,d,2,3dfc
  //   ,d,1601,4afc,180,de,d,16c2,1fc,f200,45f8,48e4,d,45f4,48e8,d,45e8
  //   ,48f4,d,45e4,48f8,d,18c2,0,19c2,fc,f800,12,1801,c6,fc,f800,1c11
  //   ,5,1ac2,1c01,190,5,1bc2,1c01,280,1cc2,1601,1a0,16c2,fc,f300,45f0
  //   ,48ec,d,1c01,1b0,1b01,c6,1c01,2a0,1cd2,1a01,6dfc,c6,1915,fbe0
  //   ,1881,414,11e0,1821,b14,c6e0,1601,1841,18c2,1fc,f900,1861,18c2
  //   ,1fc,f900,16c2,fc,f900,12,414,e4e0,100,b14,dee0,12,180,1dc2,1801
  //   ,85,18c2,a3e8,a5,a5fc,45,25,2,8030,5,1981,1d11,85,19c2,1fc,f200
  //   ,414,62e0,1601,2a0,16c2,cbfc,f600,1581,afe8,2315,22e1,12,180,1dc2
  //   ,1801,c1e8,a5,18c2,c4fc,45,18c2,25,2,8030,1901,a5,1d11,a5,19c2
  //   ,f200,1fc,1715,414,7e0,1dc2,1601,280,1ac2,1701,1bc2,1d11,5,2a0
  //   ,16c2,1d01,190,5,17d6,1fc,f300,1c81,1cc2,1fc,f900,414,18e0,1dc2
  //   ,414,26e0,1dc2,414,35e0,1801,414,41e0,414,4ce0,414,57e0,1dc2,414
  //   ,6de0,1dc2,414,7ae0,414,86e0,414,91e0,414,9ce0,1dc2,1a01,2a0,16c2
  //   ,1b01,17c2,314,cbe0,f600,1601,280,18c2,1701,19c2,1d01,16c2,314
  //   ,e0,f400,2,18c2,0,19c2,314,cbe0,f500,1881,18c2,1ee8,1da1,20fc
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endmodule
