// Digital circuit gigatroncpu.dig as structural Verilog
module gigatroncpu (
  input  CLK_25MHz,
  input  CLK_6250KHz,
  input  nRESET,
  input  [15:0] ROMDATA,
  input  [7:0] SRAMDATAREAD,
  input  SER_DATA,
  output [15:0] ROMAddress,
  output [7:0] EXOUT,
  output [15:0] SRAMAddress,
  output [7:0] SRAMDATAWRITE,
  output nOE_SRAM,
  output nWE_SRAM,
  output [3:0] VGA_R,
  output [3:0] VGA_G,
  output [3:0] VGA_B,
  output VGA_HS,
  output VGA_VS,
  output SER_PULSE,
  output SER_LATCH,
  output [7:0] RegIR,
  output [7:0] RegDR,
  output [7:0] RegAccu,
  output [7:0] RegX,
  output [7:0] RegY,
  output [7:0] RegOUT,
  output [7:0] BUSValue,
  output [7:0] ALUValue,
  output [7:0] Input,
  output nIE
);

  wire _7432_1_pin12, _74283_1_pin9, AL, AR0, AR1, AR2, AR3, CO, EH, EL, INV_A_IN, INV_A_OUT, INV_B_IN,
       INV_B_OUT, INV_C_IN, INV_C_OUT, JUMP_INSN, LD_INSN, Logic_Unit_0_pin7, Logic_Unit_0_pin9,
       Logic_Unit_1_pin7, Logic_Unit_1_pin9, Logic_Unit_2_pin7, Logic_Unit_2_pin9, Logic_Unit_3_pin7,
       Logic_Unit_3_pin9, Logic_Unit_4_pin7, Logic_Unit_4_pin9, Logic_Unit_5_pin7, Logic_Unit_5_pin9,
       Logic_Unit_6_pin7, Logic_Unit_6_pin9, Logic_Unit_7_pin7, Logic_Unit_7_pin9, Mode_Decoder_ny0,
       Mode_Decoder_ny1, Mode_Decoder_ny2, Mode_Decoder_ny3, Mode_Decoder_ny6, nAE, nAL, nAR0, nAR1, nAR2,
       nAR3, nDE, nLD, nOL, nXL, nYL, OL_INSN, Operation_Decoder_ny0, Operation_Decoder_ny1,
       Operation_Decoder_ny2, Operation_Decoder_ny3, Operation_Decoder_ny4, Operation_Decoder_ny5,
       PC_0_3_pin15, PC_4_7_pin15, PC_8_11_pin15, PH, PL, X_register_high_pin10;
  wire [7:0] AEBUS, and_1_out, and_2_out, and_3_out, and_4_out, and_10_out, DEBUS;

  _74153 Logic_Unit_3 (
    .pin1(1'b0), .pin2(BUSValue[3]), .pin3(AR3), .pin4(AR2), .pin5(AR1), .pin6(AR0),
    .pin7(Logic_Unit_3_pin7), .pin8(1'b0), .pin9(Logic_Unit_3_pin9), .pin10(1'b0), .pin11(1'b1),
    .pin12(1'b0), .pin13(1'b1), .pin14(RegAccu[3]), .pin15(AL), .pin16(1'b1));
  _74153 Logic_Unit_4 (
    .pin1(AL), .pin2(RegAccu[4]), .pin3(1'b1), .pin4(1'b1), .pin5(1'b0), .pin6(1'b0),
    .pin7(Logic_Unit_4_pin7), .pin8(1'b0), .pin9(Logic_Unit_4_pin9), .pin10(AR0), .pin11(AR2), .pin12(AR1),
    .pin13(AR3), .pin14(BUSValue[4]), .pin15(1'b0), .pin16(1'b1));
  _74161 PC_0_3 (
    .pin1(nRESET), .pin2(CLK_25MHz), .pin3(BUSValue[0]), .pin4(BUSValue[1]), .pin5(BUSValue[2]),
    .pin6(BUSValue[3]), .pin7(1'b1), .pin8(1'b0), .pin9(PL), .pin10(1'b1), .pin11(ROMAddress[3]),
    .pin12(ROMAddress[2]), .pin13(ROMAddress[1]), .pin14(ROMAddress[0]), .pin15(PC_0_3_pin15), .pin16(1'b1));
  _74273 Data_Register_DR (
    .pin1(1'b1), .pin2(RegDR[7]), .pin3(ROMDATA[15]), .pin4(ROMDATA[13]), .pin5(RegDR[5]), .pin6(RegDR[3]),
    .pin7(ROMDATA[11]), .pin8(ROMDATA[9]), .pin9(RegDR[1]), .pin10(1'b0), .pin11(CLK_25MHz),
    .pin12(RegDR[0]), .pin13(ROMDATA[8]), .pin14(ROMDATA[10]), .pin15(RegDR[2]), .pin16(RegDR[4]),
    .pin17(ROMDATA[12]), .pin18(ROMDATA[14]), .pin19(RegDR[6]), .pin20(1'b1));
  _74377 Accumulator (
    .pin1(nLD), .pin2(RegAccu[3]), .pin3(ALUValue[3]), .pin4(ALUValue[2]), .pin5(RegAccu[2]),
    .pin6(RegAccu[1]), .pin7(ALUValue[1]), .pin8(ALUValue[0]), .pin9(RegAccu[0]), .pin10(1'b0),
    .pin11(CLK_6250KHz), .pin12(RegAccu[5]), .pin13(ALUValue[5]), .pin14(ALUValue[4]), .pin15(RegAccu[4]),
    .pin16(RegAccu[7]), .pin17(ALUValue[7]), .pin18(ALUValue[6]), .pin19(RegAccu[6]), .pin20(1'b1));
  _74138ndelay Operation_Decoder (
    .A(RegIR[5]), .B(RegIR[6]), .C(RegIR[7]), .G(1'b1), .nGB(1'b0), .nGA(1'b0), .nY0(Operation_Decoder_ny0),
    .nY1(Operation_Decoder_ny1), .nY2(Operation_Decoder_ny2), .nY3(Operation_Decoder_ny3),
    .nY4(Operation_Decoder_ny4), .nY5(Operation_Decoder_ny5), .nY6(INV_B_IN), .nY7(JUMP_INSN), .VCC(1'b1),
    .GND(1'b0));
  _74153 Condition_Decoder (
    .pin1(JUMP_INSN), .pin2(CO), .pin3(1'b0), .pin4(RegIR[4]), .pin5(RegIR[3]), .pin6(RegIR[2]),
    .pin7(INV_C_IN), .pin8(1'b0), .pin10(1'b1), .pin11(1'b1), .pin12(1'b1), .pin13(1'b1), .pin14(RegAccu[7]),
    .pin15(1'b1), .pin16(1'b1));  // open: pin9
  _74377 Output_register (
    .pin1(nOL), .pin2(RegOUT[3]), .pin3(ALUValue[3]), .pin4(ALUValue[2]), .pin5(RegOUT[2]), .pin6(RegOUT[1]),
    .pin7(ALUValue[1]), .pin8(ALUValue[0]), .pin9(RegOUT[0]), .pin10(1'b0), .pin11(CLK_6250KHz),
    .pin12(RegOUT[4]), .pin13(ALUValue[4]), .pin14(ALUValue[5]), .pin15(RegOUT[5]), .pin16(RegOUT[6]),
    .pin17(ALUValue[6]), .pin18(ALUValue[7]), .pin19(RegOUT[7]), .pin20(1'b1));
  _74273 _74273_1 (
    .pin1(1'b1), .pin2(EXOUT[0]), .pin3(RegAccu[3]), .pin4(RegAccu[2]), .pin5(EXOUT[1]), .pin6(EXOUT[2]),
    .pin7(RegAccu[1]), .pin8(RegAccu[0]), .pin9(EXOUT[3]), .pin10(1'b0), .pin11(RegOUT[6]), .pin12(EXOUT[4]),
    .pin13(RegAccu[4]), .pin14(RegAccu[5]), .pin15(EXOUT[5]), .pin16(EXOUT[6]), .pin17(RegAccu[6]),
    .pin18(RegAccu[7]), .pin19(EXOUT[7]), .pin20(1'b1));
  assign and_1_out = DEBUS & ~{8{nDE}};  // And and_1, 8 bits wide
  assign and_2_out = Input & ~{8{nIE}};  // And and_2, 8 bits wide
  assign and_3_out = AEBUS & ~{8{nAE}};  // And and_3, 8 bits wide
  assign and_4_out = SRAMDATAREAD & ~{8{nOE_SRAM}};  // And and_4, 8 bits wide
  _74157 _74157_1 (
    .pin1(EL), .pin2(RegX[4]), .pin3(RegDR[4]), .pin4(SRAMAddress[4]), .pin5(RegX[5]), .pin6(RegDR[5]),
    .pin7(SRAMAddress[5]), .pin8(1'b0), .pin9(SRAMAddress[6]), .pin10(RegDR[6]), .pin11(RegX[6]),
    .pin12(SRAMAddress[7]), .pin13(RegDR[7]), .pin14(RegX[7]), .pin15(1'b0), .pin16(1'b1));
  _74157 _74157_2 (
    .pin1(EL), .pin2(RegX[1]), .pin3(RegDR[1]), .pin4(SRAMAddress[1]), .pin5(RegX[2]), .pin6(RegDR[2]),
    .pin7(SRAMAddress[2]), .pin8(1'b0), .pin9(SRAMAddress[3]), .pin10(RegDR[3]), .pin11(RegX[3]),
    .pin12(SRAMAddress[0]), .pin13(RegDR[0]), .pin14(RegX[0]), .pin15(1'b0), .pin16(1'b1));
  _74157 _74157_3 (
    .pin1(1'b0), .pin2(RegY[5]), .pin3(1'b1), .pin4(SRAMAddress[13]), .pin5(RegY[6]), .pin6(1'b1),
    .pin7(SRAMAddress[14]), .pin8(1'b0), .pin9(SRAMAddress[11]), .pin10(1'b1), .pin11(RegY[3]),
    .pin12(SRAMAddress[9]), .pin13(1'b1), .pin14(RegY[1]), .pin15(EH), .pin16(1'b1));
  _74157 _74157_4 (
    .pin1(1'b0), .pin2(RegY[0]), .pin3(1'b1), .pin4(SRAMAddress[8]), .pin5(RegY[7]), .pin6(1'b1),
    .pin7(SRAMAddress[15]), .pin8(1'b0), .pin9(SRAMAddress[10]), .pin10(1'b1), .pin11(RegY[2]),
    .pin12(SRAMAddress[12]), .pin13(1'b1), .pin14(RegY[4]), .pin15(EH), .pin16(1'b1));
  _74153 Logic_Unit_2 (
    .pin1(1'b0), .pin2(BUSValue[2]), .pin3(AR3), .pin4(AR2), .pin5(AR1), .pin6(AR0),
    .pin7(Logic_Unit_2_pin7), .pin8(1'b0), .pin9(Logic_Unit_2_pin9), .pin10(1'b0), .pin11(1'b1),
    .pin12(1'b0), .pin13(1'b1), .pin14(RegAccu[2]), .pin15(AL), .pin16(1'b1));
  _74153 Logic_Unit_5 (
    .pin1(AL), .pin2(RegAccu[5]), .pin3(1'b1), .pin4(1'b1), .pin5(1'b0), .pin6(1'b0),
    .pin7(Logic_Unit_5_pin7), .pin8(1'b0), .pin9(Logic_Unit_5_pin9), .pin10(AR0), .pin11(AR2), .pin12(AR1),
    .pin13(AR3), .pin14(BUSValue[5]), .pin15(1'b0), .pin16(1'b1));
  _74161 PC_4_7 (
    .pin1(nRESET), .pin2(CLK_25MHz), .pin3(BUSValue[4]), .pin4(BUSValue[5]), .pin5(BUSValue[6]),
    .pin6(BUSValue[7]), .pin7(1'b1), .pin8(1'b0), .pin9(PL), .pin10(PC_0_3_pin15), .pin11(ROMAddress[7]),
    .pin12(ROMAddress[6]), .pin13(ROMAddress[5]), .pin14(ROMAddress[4]), .pin15(PC_4_7_pin15), .pin16(1'b1));
  _7414 Buffer_Inverter_1 (
    .pin1(nAR0), .pin2(AR0), .pin3(nAR1), .pin4(AR1), .pin5(nAR2), .pin6(AR2), .pin7(1'b0), .pin8(INV_B_OUT),
    .pin9(INV_B_IN), .pin10(INV_A_OUT), .pin11(INV_A_IN), .pin12(AR3), .pin13(nAR3), .pin14(1'b1));
  _74273 Instruction_Register_IR (
    .pin1(1'b1), .pin2(RegIR[7]), .pin3(ROMDATA[7]), .pin4(ROMDATA[4]), .pin5(RegIR[4]), .pin6(RegIR[3]),
    .pin7(ROMDATA[3]), .pin8(ROMDATA[0]), .pin9(RegIR[0]), .pin10(1'b0), .pin11(CLK_25MHz), .pin12(RegIR[1]),
    .pin13(ROMDATA[1]), .pin14(ROMDATA[2]), .pin15(RegIR[2]), .pin16(RegIR[5]), .pin17(ROMDATA[5]),
    .pin18(ROMDATA[6]), .pin19(RegIR[6]), .pin20(1'b1));
  _74161 X_register_high (
    .pin1(1'b1), .pin2(CLK_6250KHz), .pin3(ALUValue[4]), .pin4(ALUValue[5]), .pin5(ALUValue[6]),
    .pin6(ALUValue[7]), .pin7(INV_A_OUT), .pin8(1'b0), .pin9(nXL), .pin10(X_register_high_pin10),
    .pin11(RegX[7]), .pin12(RegX[6]), .pin13(RegX[5]), .pin14(RegX[4]), .pin16(1'b1));  // open: pin15
  _74161 X_register_low (
    .pin1(1'b1), .pin2(CLK_6250KHz), .pin3(ALUValue[0]), .pin4(ALUValue[1]), .pin5(ALUValue[2]),
    .pin6(ALUValue[3]), .pin7(INV_A_OUT), .pin8(1'b0), .pin9(nXL), .pin10(1'b1), .pin11(RegX[3]),
    .pin12(RegX[2]), .pin13(RegX[1]), .pin14(RegX[0]), .pin15(X_register_high_pin10), .pin16(1'b1));
  and and_5 (nAL, RegIR[7], JUMP_INSN);
  assign BUSValue = and_1_out | and_2_out | and_3_out | and_4_out;  // Or or_1, 8 bits wide
  and and_6 (nAR0, Operation_Decoder_ny5, JUMP_INSN);
  _74595 Game_Controller_Input (
    .pin1(Input[1]), .pin2(Input[2]), .pin3(Input[3]), .pin4(Input[4]), .pin5(Input[5]), .pin6(Input[6]),
    .pin7(Input[7]), .pin8(1'b0), .pin10(1'b1), .pin11(RegOUT[6]), .pin12(RegOUT[6]), .pin13(nIE),
    .pin14(SER_DATA), .pin15(Input[0]), .pin16(1'b1));  // open: pin9
  _74244 BUS_Gateway_AC (
    .pin1(nAE), .pin2(RegAccu[0]), .pin3(AEBUS[4]), .pin4(RegAccu[1]), .pin5(AEBUS[5]), .pin6(RegAccu[2]),
    .pin7(AEBUS[6]), .pin8(RegAccu[3]), .pin9(AEBUS[7]), .pin10(1'b0), .pin11(RegAccu[7]), .pin12(AEBUS[3]),
    .pin13(RegAccu[6]), .pin14(AEBUS[2]), .pin15(RegAccu[5]), .pin16(AEBUS[1]), .pin17(RegAccu[4]),
    .pin18(AEBUS[0]), .pin19(nAE), .pin20(1'b1));
  _74153 Logic_Unit_1 (
    .pin1(1'b0), .pin2(BUSValue[1]), .pin3(AR3), .pin4(AR2), .pin5(AR1), .pin6(AR0),
    .pin7(Logic_Unit_1_pin7), .pin8(1'b0), .pin9(Logic_Unit_1_pin9), .pin10(1'b0), .pin11(1'b1),
    .pin12(1'b0), .pin13(1'b1), .pin14(RegAccu[1]), .pin15(AL), .pin16(1'b1));
  _74153 Logic_Unit_6 (
    .pin1(AL), .pin2(RegAccu[6]), .pin3(1'b1), .pin4(1'b1), .pin5(1'b0), .pin6(1'b0),
    .pin7(Logic_Unit_6_pin7), .pin8(1'b0), .pin9(Logic_Unit_6_pin9), .pin10(AR0), .pin11(AR2), .pin12(AR1),
    .pin13(AR3), .pin14(BUSValue[6]), .pin15(1'b0), .pin16(1'b1));
  and and_7 (nAR1, Operation_Decoder_ny2, Operation_Decoder_ny3, Operation_Decoder_ny5);
  and and_8 (nAR2, Operation_Decoder_ny0, Operation_Decoder_ny2, Operation_Decoder_ny3, Operation_Decoder_ny4, JUMP_INSN);
  _74161 PC_8_11 (
    .pin1(nRESET), .pin2(CLK_25MHz), .pin3(RegY[0]), .pin4(RegY[1]), .pin5(RegY[2]), .pin6(RegY[3]),
    .pin7(PL), .pin8(1'b0), .pin9(PH), .pin10(PC_4_7_pin15), .pin11(ROMAddress[11]), .pin12(ROMAddress[10]),
    .pin13(ROMAddress[9]), .pin14(ROMAddress[8]), .pin15(PC_8_11_pin15), .pin16(1'b1));
  and and_9 (nAR3, Operation_Decoder_ny0, Operation_Decoder_ny1, Operation_Decoder_ny2, Operation_Decoder_ny4);
  _7414 Buffer_Inverter_2 (
    .pin1(INV_C_IN), .pin2(INV_C_OUT), .pin3(nAL), .pin4(AL), .pin5(1'b0), .pin7(1'b0), .pin9(1'b0),
    .pin11(1'b0), .pin13(1'b0), .pin14(1'b1));  // open: pin6, pin8, pin10, pin12
  _74244 Non_inverting_tri_state_buffer (
    .pin1(nDE), .pin2(RegDR[6]), .pin3(DEBUS[4]), .pin4(RegDR[7]), .pin5(DEBUS[2]), .pin6(RegDR[5]),
    .pin7(DEBUS[0]), .pin8(RegDR[3]), .pin9(DEBUS[1]), .pin10(1'b0), .pin11(RegDR[1]), .pin12(DEBUS[3]),
    .pin13(RegDR[0]), .pin14(DEBUS[5]), .pin15(RegDR[2]), .pin16(DEBUS[7]), .pin17(RegDR[4]),
    .pin18(DEBUS[6]), .pin19(nDE), .pin20(1'b1));
  _74377 Y_register (
    .pin1(nYL), .pin2(RegY[0]), .pin3(ALUValue[0]), .pin4(ALUValue[1]), .pin5(RegY[1]), .pin6(RegY[2]),
    .pin7(ALUValue[2]), .pin8(ALUValue[3]), .pin9(RegY[3]), .pin10(1'b0), .pin11(CLK_6250KHz),
    .pin12(RegY[7]), .pin13(ALUValue[7]), .pin14(ALUValue[6]), .pin15(RegY[6]), .pin16(RegY[5]),
    .pin17(ALUValue[5]), .pin18(ALUValue[4]), .pin19(RegY[4]), .pin20(1'b1));
  _74153 Logic_Unit_0 (
    .pin1(1'b0), .pin2(BUSValue[0]), .pin3(AR3), .pin4(AR2), .pin5(AR1), .pin6(AR0),
    .pin7(Logic_Unit_0_pin7), .pin8(1'b0), .pin9(Logic_Unit_0_pin9), .pin10(1'b0), .pin11(1'b1),
    .pin12(1'b0), .pin13(1'b1), .pin14(RegAccu[0]), .pin15(AL), .pin16(1'b1));
  _74153 Logic_Unit_7 (
    .pin1(AL), .pin2(RegAccu[7]), .pin3(1'b1), .pin4(1'b1), .pin5(1'b0), .pin6(1'b0),
    .pin7(Logic_Unit_7_pin7), .pin8(1'b0), .pin9(Logic_Unit_7_pin9), .pin10(AR0), .pin11(AR2), .pin12(AR1),
    .pin13(AR3), .pin14(BUSValue[7]), .pin15(1'b0), .pin16(1'b1));
  assign and_10_out = BUSValue & ~{8{nWE_SRAM}};  // And and_10, 8 bits wide
  assign SRAMDATAWRITE = ~nWE_SRAM ? and_10_out : 8'bz;  // DriverInvSel driverinvsel_1
  _74161 PC_8_12 (
    .pin1(nRESET), .pin2(CLK_25MHz), .pin3(RegY[4]), .pin4(RegY[5]), .pin5(RegY[6]), .pin6(RegY[7]),
    .pin7(PL), .pin8(1'b0), .pin9(PH), .pin10(PC_8_11_pin15), .pin11(ROMAddress[15]), .pin12(ROMAddress[14]),
    .pin13(ROMAddress[13]), .pin14(ROMAddress[12]), .pin16(1'b1));  // open: pin15
  _74138ndelay Mode_Decoder (
    .A(RegIR[2]), .B(RegIR[3]), .C(RegIR[4]), .G(JUMP_INSN), .nGB(1'b0), .nGA(1'b0), .nY0(Mode_Decoder_ny0),
    .nY1(Mode_Decoder_ny1), .nY2(Mode_Decoder_ny2), .nY3(Mode_Decoder_ny3), .nY4(nXL), .nY5(nYL),
    .nY6(Mode_Decoder_ny6), .nY7(INV_A_IN), .VCC(1'b1), .GND(1'b0));
  _7432 _7432_1 (
    .pin1(CLK_25MHz), .pin2(INV_B_IN), .pin3(nWE_SRAM), .pin4(OL_INSN), .pin5(INV_B_OUT), .pin6(nOL),
    .pin7(1'b0), .pin8(nLD), .pin9(LD_INSN), .pin10(INV_B_OUT), .pin11(PH), .pin12(_7432_1_pin12),
    .pin13(JUMP_INSN), .pin14(1'b1));
  and and_11 (PL, PH, INV_C_OUT);
  _74283 _74283_1 (
    .pin1(ALUValue[1]), .pin2(Logic_Unit_1_pin9), .pin3(Logic_Unit_1_pin7), .pin4(ALUValue[0]),
    .pin5(Logic_Unit_0_pin7), .pin6(Logic_Unit_0_pin9), .pin7(AR0), .pin8(1'b0), .pin9(_74283_1_pin9),
    .pin10(ALUValue[3]), .pin11(Logic_Unit_3_pin9), .pin12(Logic_Unit_3_pin7), .pin13(ALUValue[2]),
    .pin14(Logic_Unit_2_pin7), .pin15(Logic_Unit_2_pin9), .pin16(1'b1));
  _74283 _74283_2 (
    .pin1(ALUValue[5]), .pin2(Logic_Unit_5_pin7), .pin3(Logic_Unit_5_pin9), .pin4(ALUValue[4]),
    .pin5(Logic_Unit_4_pin7), .pin6(Logic_Unit_4_pin9), .pin7(_74283_1_pin9), .pin8(1'b0), .pin9(CO),
    .pin10(ALUValue[7]), .pin11(Logic_Unit_7_pin9), .pin12(Logic_Unit_7_pin7), .pin13(ALUValue[6]),
    .pin14(Logic_Unit_6_pin9), .pin15(Logic_Unit_6_pin7), .pin16(1'b1));
  and and_12 (LD_INSN, Mode_Decoder_ny0, Mode_Decoder_ny1, Mode_Decoder_ny2, Mode_Decoder_ny3);
  and and_13 (OL_INSN, Mode_Decoder_ny6, INV_A_IN);
  and and_14 (EL, Mode_Decoder_ny1, Mode_Decoder_ny3, INV_A_IN);
  _74139 Bus_access_decoder_and_16_Bit_jump__JMP__decoder (
    .pin1(1'b0), .pin2(RegIR[0]), .pin3(RegIR[1]), .pin4(nDE), .pin5(nOE_SRAM), .pin6(nAE), .pin7(nIE),
    .pin8(1'b0), .pin12(_7432_1_pin12), .pin13(RegIR[2]), .pin14(RegIR[3]), .pin15(RegIR[4]), .pin16(1'b1));  // open: pin9, pin10, pin11
  and and_15 (EH, Mode_Decoder_ny2, Mode_Decoder_ny3, INV_A_IN);

  assign SER_LATCH = RegOUT[7];
  assign SER_PULSE = RegOUT[6];
  assign VGA_B = {RegOUT[5:4], 2'b00};
  assign VGA_G = {RegOUT[3:2], 2'b00};
  assign VGA_HS = RegOUT[6];
  assign VGA_R = {RegOUT[1:0], 2'b00};
  assign VGA_VS = RegOUT[7];

  // Other names for the same wires on the sheet: BUS[7:0] = BUSValue; BUS0 = BUSValue[0]; BUS1 = BUSValue[1];
  //   BUS2 = BUSValue[2]; BUS3 = BUSValue[3]; BUS4 = BUSValue[4]; BUS5 = BUSValue[5]; BUS6 = BUSValue[6];
  //   BUS7 = BUSValue[7]; AC0 = RegAccu[0]; ACBUS[7:0] = RegAccu; AC1 = RegAccu[1]; AC2 = RegAccu[2];
  //   AC3 = RegAccu[3]; AC4 = RegAccu[4]; AC5 = RegAccu[5]; AC6 = RegAccu[6]; AC7 = RegAccu[7]; ALU0 = ALUValue[0];
  //   ALUBUS[7:0] = ALUValue; ALU1 = ALUValue[1]; ALU2 = ALUValue[2]; ALU3 = ALUValue[3]; ALU4 = ALUValue[4];
  //   ALU5 = ALUValue[5]; ALU6 = ALUValue[6]; ALU7 = ALUValue[7]; CLK1 = CLK_25MHz; CLK2 = CLK_6250KHz; D0 = RegDR[0];
  //   DRBUS[7:0] = RegDR; D1 = RegDR[1]; D2 = RegDR[2]; D3 = RegDR[3]; D4 = RegDR[4]; D5 = RegDR[5]; D6 = RegDR[6];
  //   D7 = RegDR[7]; DQ0 = ROMDATA[0]; DQBUS[15:0] = ROMDATA; DQ1 = ROMDATA[1]; DQ2 = ROMDATA[2]; DQ3 = ROMDATA[3];
  //   DQ4 = ROMDATA[4]; DQ5 = ROMDATA[5]; DQ6 = ROMDATA[6]; DQ7 = ROMDATA[7]; DQ8 = ROMDATA[8]; DQ9 = ROMDATA[9];
  //   DQ10 = ROMDATA[10]; DQ11 = ROMDATA[11]; DQ12 = ROMDATA[12]; DQ13 = ROMDATA[13]; DQ14 = ROMDATA[14];
  //   DQ15 = ROMDATA[15]; EXOUTBUS[7:0] = EXOUT; IEBUS[7:0] = Input; IEBUS0 = Input[0]; IEBUS1 = Input[1];
  //   IEBUS2 = Input[2]; IEBUS3 = Input[3]; IEBUS4 = Input[4]; IEBUS5 = Input[5]; IEBUS6 = Input[6];
  //   IEBUS7 = Input[7]; IR0 = RegIR[0]; IRBUS[7:0] = RegIR; IR1 = RegIR[1]; IR2 = RegIR[2]; IR3 = RegIR[3];
  //   IR4 = RegIR[4]; IR5 = RegIR[5]; IR6 = RegIR[6]; IR7 = RegIR[7]; IX = INV_A_OUT; nOE = nOE_SRAM; nRST = nRESET;
  //   nWE = nWE_SRAM; OEBUS[7:0] = SRAMDATAREAD; OUT0 = RegOUT[0]; OUTBUS[7:0] = RegOUT; OUT1 = RegOUT[1];
  //   OUT2 = RegOUT[2]; OUT3 = RegOUT[3]; OUT4 = RegOUT[4]; OUT5 = RegOUT[5]; OUT6 = RegOUT[6]; OUT7 = RegOUT[7];
  //   PC0 = ROMAddress[0]; PCBUS[15:0] = ROMAddress; PC1 = ROMAddress[1]; PC2 = ROMAddress[2]; PC3 = ROMAddress[3];
  //   PC4 = ROMAddress[4]; PC5 = ROMAddress[5]; PC6 = ROMAddress[6]; PC7 = ROMAddress[7]; PC8 = ROMAddress[8];
  //   PC9 = ROMAddress[9]; PC10 = ROMAddress[10]; PC11 = ROMAddress[11]; PC12 = ROMAddress[12]; PC13 = ROMAddress[13];
  //   PC14 = ROMAddress[14]; PC15 = ROMAddress[15]; SRAM_A0 = SRAMAddress[0]; SRAMADDRESSBUS[15:0] = SRAMAddress;
  //   SRAM_A1 = SRAMAddress[1]; SRAM_A2 = SRAMAddress[2]; SRAM_A3 = SRAMAddress[3]; SRAM_A4 = SRAMAddress[4];
  //   SRAM_A5 = SRAMAddress[5]; SRAM_A6 = SRAMAddress[6]; SRAM_A7 = SRAMAddress[7]; SRAM_A8 = SRAMAddress[8];
  //   SRAM_A9 = SRAMAddress[9]; SRAM_A10 = SRAMAddress[10]; SRAM_A11 = SRAMAddress[11]; SRAM_A12 = SRAMAddress[12];
  //   SRAM_A13 = SRAMAddress[13]; SRAM_A14 = SRAMAddress[14]; SRAM_A15 = SRAMAddress[15]; WEBUS[7:0] = SRAMDATAWRITE;
  //   X0 = RegX[0]; XBUS[7:0] = RegX; X1 = RegX[1]; X2 = RegX[2]; X3 = RegX[3]; X4 = RegX[4]; X5 = RegX[5];
  //   X6 = RegX[6]; X7 = RegX[7]; Y0 = RegY[0]; YBUS[7:0] = RegY; Y1 = RegY[1]; Y2 = RegY[2]; Y3 = RegY[3];
  //   Y4 = RegY[4]; Y5 = RegY[5]; Y6 = RegY[6]; Y7 = RegY[7]

  // Notes on the sheet:
  //   CLK_25MHz: Hz: 5000
  //   ROMAddress: Current address in ROM. Next instruction is fetched from this address.
  //   EXOUT: Bit 0 to 3 are LEDs. Bit 4 to 7 is Audio out.
  //   SRAMAddress: SRAM address. A15 is not used in original Gigatron TTL schematic.
  //   SRAMDATAWRITE: Data written to SRAM.
  //   nOE_SRAM: Control line for reading SRAM.
  //   nWE_SRAM: Control line for writing SRAM.
  //   VGA_R: VGA red output.
  //   VGA_G: VGA green output.
  //   VGA_B: VGA blue output.
  //   SER_PULSE: Sub-D pol 9, pin 4 of Famiclone game controller
  //   SER_LATCH: Sub-D pol 9, pin 3 of Famiclone game controller
  //   RegIR: Instruction Register Value
  //   RegDR: Data Register Value
  //   RegAccu: Accumulator Register Value
  //   RegX: X Register Value
  //   nRESET: default 1
  //   RegY: Y Register Value
  //   RegOUT: OUT Register Value
  //   BUSValue: Value on internal BUS.
  //   ROMDATA: Data in ROM. This is the next instruction executed., default 3860
  //   SRAMDATAREAD: Data read from SRAM.
  //   ALUValue: Current value calculated by ALU.
  //   Input: Input data read from gamepad (for debugging).
  //   nIE: Control line for reading data from gamepad (for debugging).
  //   SER_DATA: Sub-D pol 9, pin 2 of Famiclone game controller
  //   Gigatron TTL CPU
  //   Pins
  //   Debug Pins
  //   Program Counter
  //   Instruction Decoding
  //   ALU
  //   Register
  //   Input/Output Register
  //   SRAM Adress Decoder
  //   BUS Translation
  //   BUS Arbiter
  //   JUMP
  //   LOAD
  //   AND
  //   OR
  //   XOR
  //   ADD
  //   SUB
  //   STORE
  //   [Y, X++], OUT
  //   VGA
  //   [D], AC
  //   [X], AC
  //   [Y, D], AC
  //   [Y, X], AC
  //   [D], X
  //   [D], Y
  //   [D], OUT
endmodule
