// Digital circuit gigatronkeyboard.dig as structural Verilog
// Keyboard for gigtron.
module gigatronkeyboard (
  input  nLD,
  output [7:0] KCODE,
  output O
);

  wire and_1_out, comparator_1_eq, comparator_2_gt, comparator_3_lt, comparator_4_eq, comparator_5_eq,
       comparator_6_eq, comparator_7_eq, comparator_8_eq, keyboard_1_av, or_1_out, priorityencoder_1_any;
  wire [2:0] priorityencoder_1_num;
  wire [7:0] keyboard_1_d, multiplexer_1_out;
  wire [15:8] keyboard_1_d_2;

  Keyboard keyboard_1 (.C(nLD), .en(1'b1), .D({keyboard_1_d_2, keyboard_1_d}), .av(keyboard_1_av));
  Comparator #(.Bits(16)) comparator_1 (
    .a({keyboard_1_d_2, keyboard_1_d}), .b(16'ha), .eq(comparator_1_eq));  // open: gt, lt
  Comparator #(.Bits(16)) comparator_2 (
    .a({keyboard_1_d_2, keyboard_1_d}), .b(16'h1f), .gt(comparator_2_gt));  // open: eq, lt
  Comparator #(.Bits(16)) comparator_3 (
    .a({keyboard_1_d_2, keyboard_1_d}), .b(16'h80), .lt(comparator_3_lt));  // open: gt, eq
  Comparator #(.Bits(16)) comparator_4 (
    .a({keyboard_1_d_2, keyboard_1_d}), .b(16'h11), .eq(comparator_4_eq));  // open: gt, lt
  Comparator #(.Bits(16)) comparator_5 (
    .a({keyboard_1_d_2, keyboard_1_d}), .b(16'h12), .eq(comparator_5_eq));  // open: gt, lt
  Comparator #(.Bits(16)) comparator_6 (
    .a({keyboard_1_d_2, keyboard_1_d}), .b(16'h13), .eq(comparator_6_eq));  // open: gt, lt
  Comparator #(.Bits(16)) comparator_7 (
    .a({keyboard_1_d_2, keyboard_1_d}), .b(16'h14), .eq(comparator_7_eq));  // open: gt, lt
  Comparator #(.Bits(16)) comparator_8 (
    .a({keyboard_1_d_2, keyboard_1_d}), .b(16'h8), .eq(comparator_8_eq));  // open: gt, lt
  or or_1 (or_1_out, comparator_1_eq, comparator_2_gt);
  and and_1 (and_1_out, keyboard_1_av, or_1_out, comparator_3_lt);
  PriorityEncoder #(.Selector_Bits(3)) priorityencoder_1 (
    .in0(comparator_4_eq), .in1(comparator_5_eq), .in2(comparator_6_eq), .in3(comparator_7_eq),
    .in4(comparator_8_eq), .in5(1'b0), .in6(1'b0), .in7(1'b0), .num(priorityencoder_1_num),
    .any(priorityencoder_1_any));
  Multiplexer #(.Selector_Bits(3), .Bits(8)) multiplexer_1 (
    .sel(priorityencoder_1_num), .in_0(8'hf7), .in_1(8'hfb), .in_2(8'hfd), .in_3(8'hfe), .in_4(8'h7f),
    .in_5({8{1'b0}}), .in_6({8{1'b0}}), .in_7({8{1'b0}}), .out(multiplexer_1_out));
  Multiplexer #(.Bits(8)) multiplexer_2 (
    .sel(priorityencoder_1_any), .in_0(keyboard_1_d), .in_1(multiplexer_1_out), .out(KCODE));
  or or_2 (O, and_1_out, priorityencoder_1_any);

  // Notes on the sheet:
  //   KCODE: 8-Bit key code
  //   O: O is 1 when key is available from keyboard.
  //   nLD: Get next key from keyboard.
  //   Keyboard
endmodule
